# Fritzing sketch arduino_multiple_relais (saved by Fritzing 0.9.3b)

parts:
  Part1 = Arduino Uno (Rev3)
  U1 = 2-Channel 5v Relay Shield [package=relay-2ch5v10a]
  L1 = Bulb holder (E10) with base
  L2 = Bulb holder (E10) with base
  VCC2 = 4 x AAA Battery Mount
  VCC1 = 4 x AAA Battery Mount

nets:
  N1: Part1.D8, U1.IN1
  N2: Part1.D9_PWM, U1.IN2
  5V: Part1.5V, U1.VCC
  GND: Part1.GND, U1.GND
  N3: U1.K1-In, VCC2.+
  N4: U1.K1-On, U1.K2-In, L2.pin_2
  N5: U1.K2-On, L1.pin_2
  N6: L1.pin_1, VCC1.-

custom parts:
  2-Channel 5v Relay Shield: 2 Channel 5v Relay Shield w. 2x SPD-06VDC-SD-C
  Bulb holder (E10) with base: A bulb holder for an E10 bulb with a base.
